# Fritzing sketch bioFeebackGameController (saved by Fritzing 0.9.3b)
breadboards: 1

parts:
  Part1 = Arduino Micro (Rev3)
  R1 = Basic Flex Resistor
  R2 = Resistor [tolerance=±5% resistance=47k package="0402 [SMD]"]
  R3 = Basic Flex Resistor
  R4 = Resistor [tolerance=±5% resistance=47k package="0402 [SMD]"]
  R5 = Basic Flex Resistor
  R6 = Basic Flex Resistor
  R7 = Resistor [tolerance=±5% resistance=47k package="0402 [SMD]"]
  R8 = Resistor [tolerance=±5% resistance=47k package="0402 [SMD]"]

nets:
  N1: Part1.GND, R2.Pin_1, R4.Pin_1, R7.Pin_1, R8.Pin_1
  N2: Part1.A3, R5.Pin_2, R7.Pin_0
  N3: Part1.A2, R6.Pin_2, R8.Pin_0
  N4: Part1.A1, R3.Pin_2, R4.Pin_0
  N5: Part1.A0, R1.Pin_2, R2.Pin_0
  N6: Part1.3V3, R1.pin_1, R3.pin_1, R5.pin_1, R6.pin_1
